# Fritzing sketch weapon (saved by Fritzing 0.9.3b)

parts:
  Onderdeel1 = Arduino Due (Rev2b)
  LED1 = Infrared LED - 5mm [package="5 mm [THT]"]
  U1 = TRANSISTOR_NPN_2 [package=to-92]
  R1 = Resistor [tolerance=±5% resistance=220 package="0603 [SMD]"]
  IR1 = TSOP312.., 314.. [package=THT]
  C1 = Capacitor Polarized [package=cpol-radial-100uf-25v]
  C2 = Capacitor [package=cap-pth-small2]
  R2 = Resistor [tolerance=±5% resistance=220 package="0805 [SMD]"]
  R3 = Resistor [tolerance=±5% resistance=220 package="1206 [SMD]"]
  HC-SR04_Sensor_1 = HC-SR04 Ultrasonic Distance Sensor
  R4 = Resistor [tolerance=±5% resistance=220 package="1206 [SMD]"]
  R5 = Resistor [tolerance=±5% resistance=220 package="1206 [SMD]"]
  LED2 = RGB LED (com. anode, rbg) [package="5 mm [THT]"]
  OLED_I2C1 = OLED 128x64 I2C Monochrome Display
  RE1 = Rotary Encoder [package=THT]
  C3 = Tantalum Capacitor [capacitance="1 μF" package="A 3216 [SMD, tantalum]"]  # not connected
  C4 = Tantalum Capacitor [capacitance=1μF package="200 mil [THT, tantalum]"]
  R6 = Resistor [tolerance=±5% resistance=220 package="0603 [SMD]"]
  R7 = Resistor [tolerance=±5% resistance=220 package="0603 [SMD]"]
  R8 = Resistor [tolerance=±5% resistance=220 package="0603 [SMD]"]
  S1 = Toggle Switch [package=THT]
  S2 = Momentary Switch [package=ksa_sealed_tac_switch]
  R9 = Resistor [tolerance=±5% resistance=220 package="0603 [SMD]"]
  Onderdeel2 = NRF24L01+ Breakout Board  # not connected

nets:
  N1: Onderdeel1.A8, S2.1
  N2: Onderdeel1.A9, Onderdeel1.D52, S1.L1
  N3: Onderdeel1.A10, Onderdeel1.D53, S1.L2
  N4: Onderdeel1.A11, S2.4
  N5: Onderdeel1.DAC0, R6.Pin_0
  N6: Onderdeel1.D16/TX2, LED2.green_cathode
  N7: Onderdeel1.D20/SDA3, OLED_I2C1.SDA
  N8: Onderdeel1.D21/SCL3, OLED_I2C1.SCK
  N9: Onderdeel1.IOREF, LED1.anode, R2.Pin_0, R3.Pin_0, LED2.blue_cathode, OLED_I2C1.VDD
  5V: Onderdeel1.5V, HC-SR04_Sensor_1.VCC
  GND: Onderdeel1.GND, U1.E, IR1.Vs, C1.-, C2.1, HC-SR04_Sensor_1.GND, R5.Pin_1, OLED_I2C1.GND, RE1.EncoderPinC, C4.-, R9.Pin_1
  N10: Onderdeel1.D8_PWM, HC-SR04_Sensor_1.TRIG
  N11: Onderdeel1.D9_PWM, R4.Pin_0
  N12: Onderdeel1.D13_PWM, R8.Pin_1
  N13: Onderdeel1.D2_PWM, R7.Pin_0
  N14: Onderdeel1.D3_PWM, R1.Pin_1
  N15: Onderdeel1.D5_PWM, IR1.GND, R3.Pin_1
  N16: Onderdeel1.D42, LED2.common_anode
  N17: Onderdeel1.D44, LED2.red_cathode
  N18: LED1.cathode, U1.C
  N19: U1.B, R1.Pin_0
  N20: IR1.Data, C1.+, C2.2, R2.Pin_1
  N21: HC-SR04_Sensor_1.ECHO, R4.Pin_1, R5.Pin_0

notes:
  PN2222A

custom parts:
  Infrared LED - 5mm: A generic infrared LED (~1.2V)
