# Fritzing sketch Master (saved by Fritzing 0.9.3b)

parts:
  Onderdeel1 = Arduino Due (Rev2b)
  OLED_I2C1 = OLED 128x64 I2C Monochrome Display
  R1 = Rotary Potentiometer (Small) [maximum_resistance=100kΩ package=THT]
  Onderdeel2 = NRF24L01+ Breakout Board
  U1 = LIPO-2000mAh [package=lipo-2000]
  TP1 = TP4056 [chip_label=TP4056 package="DIP (Dual Inline) [THT]"]
  M1 = RioRand LM2596
  DFRobot_DFPlayer_Mini1 = DFRobot DFPlayer Mini [part_number=DFR0299]
  AMP1 = GF1002 Stereo Amplifier
  SP1 = SPEAKER [package=pcb_mount_speaker]
  S1 = SWITCH-DPDT [package=eg2211]
  U2 = 3.5mm Audio Jack [package=audio-jack]
  Matrix_keypad1 = KEYPAD 4x4  # not connected

nets:
  N1: Onderdeel1.D18/TX1, DFRobot_DFPlayer_Mini1.RX
  N2: Onderdeel1.D19/RX1, DFRobot_DFPlayer_Mini1.TX
  VCC: Onderdeel1.IOREF, OLED_I2C1.VDD, Onderdeel2.VCC, DFRobot_DFPlayer_Mini1.VCC
  GND: Onderdeel1.GND, OLED_I2C1.GND, Onderdeel2.GND, M1.Pin_4
  N3: Onderdeel1.VIN, M1.Pin_3
  N4: Onderdeel1.D9_PWM, R1.leg1
  N5: Onderdeel1.D10_PWM/SS0, R1.wiper
  N6: Onderdeel1.D11_PWM, R1.leg2
  N7: Onderdeel1.D12_PWM, OLED_I2C1.SDA
  N8: Onderdeel1.D13_PWM, OLED_I2C1.SCK
  N9: Onderdeel1.D2_PWM, Onderdeel2.MOSI
  N10: Onderdeel1.D3_PWM, Onderdeel2.MISO
  N11: Onderdeel1.D4_PWM/SS1, Onderdeel2.SCK
  N12: Onderdeel1.D5_PWM, Onderdeel2.CS
  N13: U1.+, S1.3
  N14: U1.-, TP1.pin5
  N15: TP1.pin3, M1.Pin_1, AMP1.POWER+
  N16: TP1.pin4, S1.6
  N17: TP1.pin6, M1.Pin_2, AMP1.POWER-
  N18: DFRobot_DFPlayer_Mini1.SPK_1, AMP1.INPUTL
  N19: DFRobot_DFPlayer_Mini1.GND-1, AMP1.INPUTG
  N20: AMP1.LOUT+, SP1.-, U2.LEFT
  N21: AMP1.LOUT-, SP1.+, U2.SLEEVE

custom parts:
  TP4056: A DIP stand-in part for whatever IC you want. With 6 pins on a 300mil dual inline package (DIP) footprint.
  GF1002 Stereo Amplifier: GF1002 6 Watt Stereo Amplifier
  KEYPAD 4x4: Matrix keypad 16 buttons, 4 rows x 4 columns
