# Fritzing sketch MasterHelper (saved by Fritzing 0.9.3b)

parts:
  Onderdeel1 = Arduino Nano (Rev3.0) (ICSP)
  Onderdeel2 = NRF24L01+ Breakout Board

nets:
  N1: Onderdeel1.D2, Onderdeel2.IRQ
  N2: Onderdeel1.D3, Onderdeel2.MISO
  N3: Onderdeel1.D4, Onderdeel2.MOSI
  N4: Onderdeel1.D5, Onderdeel2.SCK
  N5: Onderdeel1.D6, Onderdeel2.CS
  GND: Onderdeel1.GND, Onderdeel2.GND
  3V3: Onderdeel1.3V3, Onderdeel2.VCC
