# Fritzing sketch Slave (saved by Fritzing 0.9.3b)

parts:
  Onderdeel1 = Arduino Nano (Rev3.0) (ICSP)
  U1 = LIPO-110mAh [package=lipo-110]
  TP1 = TP4056 [chip_label=TP4056 package="DIP (Dual Inline) [THT]"]
  U2 = SBX DSUN [package=THT]
  LED1 = Infrared LED - 5mm [package="5 mm [THT]"]
  IR1 = TSOP312.., 314.. [package=THT]
  LED2 = smd LED [color="Red (633nm)" package="1206 [SMD]"]
  M1 = DC Motor
  RE1 = Rotary Encoder [package=THT]
  J1 = Piezo Speaker
  S1 = SPST Switch [package=switch-spdt_lock.007s]
  OLED_I2C1 = OLED 128x64 I2C Monochrome Display
  Onderdeel2 = NRF24L01+ Breakout Board  # not connected

nets:
  GND: Onderdeel1.GND, TP1.pin6, U2.GND, LED1.cathode, IR1.GND, LED2.cathode, M1.pin_2, J1.pin1, OLED_I2C1.GND
  N1: Onderdeel1.D2, LED1.anode
  N2: Onderdeel1.D3, IR1.Data
  N3: Onderdeel1.D7, OLED_I2C1.SDA
  N4: Onderdeel1.D8, OLED_I2C1.SCK
  N5: Onderdeel1.D9, S1.P
  N6: Onderdeel1.D11/MOSI, LED2.anode
  N7: Onderdeel1.VIN, U2.+VOUT
  N8: Onderdeel1.A7, J1.pin2
  N9: Onderdeel1.A3, M1.pin_1
  N10: Onderdeel1.A2, RE1.EncoderPinA
  N11: Onderdeel1.A1, RE1.EncoderPinC
  N12: Onderdeel1.A0, RE1.EncoderPinB
  3V3: Onderdeel1.3V3, IR1.Vs, S1.O, OLED_I2C1.VDD
  N13: U1.+, TP1.pin4
  N14: U1.-, TP1.pin5
  N15: TP1.pin3, U2.+VIN

notes:
  +-3,7V
  10V
  Laser

custom parts:
  TP4056: A DIP stand-in part for whatever IC you want. With 6 pins on a 300mil dual inline package (DIP) footprint.
  SBX DSUN: SBX DSUN input voltage 4.5 - 28V DC output voltage .8v to 20VDC (step down converter) Output current 3A max
  Infrared LED - 5mm: A generic infrared LED (~1.2V)
