# Fritzing sketch Schakelschema (saved by Fritzing 0.9.3b)

parts:
  Onderdeel1 = Arduino Nano (Rev3.0) (ICSP)
  U1 = LIPO-110mAh [package=lipo-110]
  TP1 = TP4056 [chip_label=TP4056 package="DIP (Dual Inline) [THT]"]
  U2 = SBX DSUN [package=THT]
  LED1 = Infrared LED - 5mm [package="5 mm [THT]"]
  IR1 = TSOP312.., 314.. [package=THT]
  U3 = FS1000A - 433Mhz RF Transmitter [package=THT]
  DFRobot_DFPlayer_Mini1 = DFRobot DFPlayer Mini [part_number=DFR0299]
  AMP1 = GF1002 Stereo Amplifier
  SP1 = SPEAKER [package=pcb_mount_speaker]
  LED2 = smd LED [color="Red (633nm)" package="1206 [SMD]"]
  M1 = DC Motor
  RE1 = Rotary Encoder [package=THT]
  J1 = Piezo Speaker
  S1 = SPST Switch [package=switch-spdt_lock.007s]
  OLED_I2C1 = OLED 128x64 I2C Monochrome Display

nets:
  N1: Onderdeel1.D1/TX, DFRobot_DFPlayer_Mini1.RX, DFRobot_DFPlayer_Mini1.IO_1
  N2: Onderdeel1.D0/RX, DFRobot_DFPlayer_Mini1.TX
  GND: Onderdeel1.GND, TP1.pin6, U2.GND, LED1.cathode, IR1.GND, U3.GND, DFRobot_DFPlayer_Mini1.GND-1, DFRobot_DFPlayer_Mini1.GND-2, AMP1.INPUTG, LED2.cathode, M1.pin_2, J1.pin1, OLED_I2C1.GND
  N3: Onderdeel1.D2, LED1.anode
  N4: Onderdeel1.D3, IR1.Data
  N5: Onderdeel1.D4, U3.DATA
  N6: Onderdeel1.D7, OLED_I2C1.SDA
  N7: Onderdeel1.D8, OLED_I2C1.SCK
  N8: Onderdeel1.D9, S1.P
  N9: Onderdeel1.D11/MOSI, LED2.anode
  N10: Onderdeel1.VIN, U2.+VOUT
  N11: Onderdeel1.A7, J1.pin2
  N12: Onderdeel1.A3, M1.pin_1
  N13: Onderdeel1.A2, RE1.EncoderPinA
  N14: Onderdeel1.A1, RE1.EncoderPinC
  N15: Onderdeel1.A0, RE1.EncoderPinB
  VCC: Onderdeel1.3V3, IR1.Vs, U3.VCC, DFRobot_DFPlayer_Mini1.VCC, S1.O, OLED_I2C1.VDD
  N16: U1.+, TP1.pin4, AMP1.POWER+
  N17: U1.-, TP1.pin5, AMP1.POWER-
  N18: TP1.pin3, U2.+VIN
  N19: DFRobot_DFPlayer_Mini1.SPK_1, AMP1.INPUTR
  N20: AMP1.ROUT-, SP1.+
  N21: AMP1.ROUT+, SP1.-

notes:
  +-3,7V
  10V
  Laser

custom parts:
  TP4056: A DIP stand-in part for whatever IC you want. With 6 pins on a 300mil dual inline package (DIP) footprint.
  SBX DSUN: SBX DSUN input voltage 4.5 - 28V DC output voltage .8v to 20VDC (step down converter) Output current 3A max
  Infrared LED - 5mm: A generic infrared LED (~1.2V)
  FS1000A - 433Mhz RF Transmitter: This is 433Mhz RF transmitter with receiver kit for Arduino ARM MCU wireless Application environment: Remote control switch, receiver module, motorcycles, automobile anti-theft products, home security products, electric doors, shutter doors, windows, remote control socket, remote control LED, remote audio remote control electric doors, garage door remote control, remote control retractable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
  GF1002 Stereo Amplifier: GF1002 6 Watt Stereo Amplifier
